// Logisim project practica3.circ as structural Verilog: 1 circuit, main circuit main
module main (
  input  p,
  input  q,
  input  r,
  input  p_2,
  input  q_2,
  input  r_2,
  input  \Se_detectó_movimiento ,
  input  Las_luces_estaban_encendidas,
  input  \Se_abrió_la_ventana ,
  input  \Decisión_Pablo ,
  input  \Decisión_Quintín ,
  input  \Decisión_Ramiro ,
  output out_13,
  output out_14,
  output Alarma_encendida,
  output \Decisión_tomada 
);

  wire and_1_out, and_2_out, and_3_out, and_4_out, and_5_out, and_6_out, and_7_out, not_1_out, not_2_out,
       not_3_out, not_4_out, not_5_out, not_6_out, not_7_out, not_8_out, or_1_out, or_2_out, or_3_out,
       or_6_out;

  not not_1 (not_1_out, p);
  not not_2 (not_2_out, q);
  not not_3 (not_3_out, r);
  not not_4 (not_4_out, q_2);
  not not_5 (not_5_out, r_2);
  not not_6 (not_6_out, \Decisión_Ramiro );
  or or_1 (or_1_out, not_1_out, q);
  or or_2 (or_2_out, not_2_out, not_3_out);
  and and_1 (and_1_out, p_2, not_4_out);
  not not_7 (not_7_out, Las_luces_estaban_encendidas);
  not not_8 (not_8_out, \Se_detectó_movimiento );
  and and_2 (and_2_out, \Decisión_Pablo , \Decisión_Quintín );
  and and_3 (and_3_out, \Decisión_Pablo , not_6_out);
  and and_4 (and_4_out, \Decisión_Quintín , not_6_out);
  or or_3 (or_3_out, or_1_out, r);
  and and_5 (and_5_out, p, or_2_out);
  or or_4 (out_14, and_1_out, not_5_out);
  and and_6 (and_6_out, \Se_detectó_movimiento , not_7_out);
  and and_7 (and_7_out, not_8_out, \Se_abrió_la_ventana );
  and and_8 (out_13, or_3_out, and_5_out);
  or or_5 (Alarma_encendida, and_6_out, and_7_out);
  or or_6 (or_6_out, and_2_out, and_3_out);
  LED led_1 (.in(Alarma_encendida));
  or or_7 (\Decisión_tomada , or_6_out, and_4_out);

  // Notes on the sheet:
  //   Estructuras Discretas 2019-1
  //   Práctica 3
  //   Mauricio Chávez Olea
  //   EJERCICIO 1
  //   EJERCICIO 2
  //   (p → q) → ¬r
  //   p ^ ¬q ↔ r v ¬p
endmodule
