// Logisim project practica4.circ as structural Verilog: 1 circuit, main circuit main
module main (
  input  p,
  input  q,
  input  r,
  input  p_2,
  input  q_2,
  input  r_2,
  input  s,
  input  \Es_ictívoro ,
  input  \Es_ictívoro_2 ,
  input  \Es_ictívoro_3 ,
  input  \Es_ictívoro_4 ,
  input  \Paula_actúa ,
  input  \Qori_actúa ,
  input  \Rosa_actúa ,
  input  \Susana_actúa ,
  input  \Teresa_actúa ,
  output out_17,
  output out_18,
  output out_19,
  output out_20
);

  wire and_1_out, and_2_out, and_3_out, and_4_out, and_5_out, and_6_out, and_7_out, and_8_out, and_9_out,
       and_10_out, and_11_out, and_12_out, and_13_out, and_14_out, and_15_out, and_16_out, and_17_out,
       and_18_out, and_19_out, and_20_out, and_21_out, and_22_out, and_23_out, and_24_out, not_1_out,
       not_2_out, not_3_out, not_4_out, not_5_out, not_6_out, not_7_out, or_2_out, or_3_out, or_4_out,
       or_6_out, or_8_out, or_9_out;

  not not_1 (not_1_out, p_2);
  not not_2 (not_2_out, q_2);
  not not_3 (not_3_out, r_2);
  and and_1 (and_1_out, not_1_out, q_2);
  and and_2 (and_2_out, not_2_out, r_2);
  and and_3 (and_3_out, not_2_out, s);
  and and_4 (and_4_out, not_2_out, not_3_out);
  and and_5 (and_5_out, \Es_ictívoro , \Es_ictívoro_2 );
  and and_6 (and_6_out, \Es_ictívoro , \Es_ictívoro_3 );
  not not_4 (not_4_out, \Paula_actúa );
  not not_5 (not_5_out, \Qori_actúa );
  not not_6 (not_6_out, \Rosa_actúa );
  not not_7 (not_7_out, \Susana_actúa );
  and and_7 (and_7_out, q, r);
  and and_8 (and_8_out, and_5_out, \Es_ictívoro_3 );
  and and_9 (and_9_out, and_5_out, \Es_ictívoro_4 );
  and and_10 (and_10_out, not_4_out, not_6_out);
  and and_11 (and_11_out, not_6_out, \Susana_actúa );
  or or_1 (out_17, p, and_7_out);
  and and_12 (and_12_out, and_1_out, s);
  and and_13 (and_13_out, not_1_out, and_4_out);
  and and_14 (and_14_out, and_6_out, \Es_ictívoro_4 );
  and and_15 (and_15_out, and_10_out, \Teresa_actúa );
  and and_16 (and_16_out, and_11_out, \Teresa_actúa );
  or or_2 (or_2_out, and_2_out, and_3_out);
  or or_3 (or_3_out, and_8_out, and_9_out);
  and and_17 (and_17_out, \Es_ictívoro_3 , \Es_ictívoro_4 );
  and and_18 (and_18_out, not_4_out, \Qori_actúa );
  and and_19 (and_19_out, not_6_out, \Susana_actúa );
  or or_4 (or_4_out, and_12_out, and_13_out);
  and and_20 (and_20_out, \Es_ictívoro_2 , and_17_out);
  and and_21 (and_21_out, not_4_out, not_5_out);
  and and_22 (and_22_out, and_21_out, and_23_out);
  and and_23 (and_23_out, not_6_out, not_7_out);
  or or_5 (out_18, or_2_out, or_4_out);
  or or_6 (or_6_out, and_20_out, and_14_out);
  and and_24 (and_24_out, and_18_out, and_19_out);
  or or_7 (out_19, or_3_out, or_6_out);
  or or_8 (or_8_out, and_24_out, and_22_out);
  or or_9 (or_9_out, and_15_out, and_16_out);
  or or_10 (out_20, or_8_out, or_9_out);

  // Notes on the sheet:
  //   pq̄r + pr̄ + qr
  //   p̄r̄s  +  q̄r̄  +  p̄qrs + q̄rs
  //   Al llegar a la pecera encontrará todo en orden
  //   Recibirá la obra al menos una buena crítica
endmodule
